// Logisim project cpu.circ as structural Verilog: 1 circuit, main circuit main
module main (
  input  [31:0] INSTRUCTION,
  input  CLOCK,
  output [31:0] FETCH_ADDRESS,
  output [31:0] s0_Value,
  output [31:0] s1_Value,
  output [31:0] s2_Value,
  output [31:0] ra_Value,
  output [31:0] HI_Value,
  output [31:0] LO_Value
);

  wire add, addi, addiu, addswitch, addu, adduswitch, ALUSrc, \and , and_4_out, and_5_out, and_8_out,
       and_9_out, and_10_out, and_12_out, and_13_out, and_14_out, and_15_out, and_16_out, and_17_out,
       and_18_out, and_19_out, and_20_out, and_21_out, and_22_out, and_23_out, and_24_out, andi, andswitch,
       beq, beqal, bne, Branch, divu, equal, ISign, j, jal, jr, Jump, lb, lbu, lhu, lui, lw,
       main_2_signed_overflow, MEM_p4, MEM_p6, MEM_p10, MEM_p12, MEM_p14, MemWr, mfhi, mflo, multu,
       not_1_out, not_2_out, not_3_out, not_4_out, not_5_out, not_6_out, not_7_out, not_8_out, not_10_out,
       not_11_out, not_12_out, not_13_out, not_14_out, not_15_out, \or , or_1_out, or_2_out, or_3_out,
       or_4_out, or_5_out, or_6_out, or_7_out, or_8_out, or_9_out, or_10_out, or_11_out, or_12_out,
       or_14_out, or_15_out, or_16_out, or_18_out, ori, orswitch, PCSrc, r_type, RegWrite, sb, sh,
       ShamtSwitch, sll, slt, slti, sltswitch, sltu, sra, srl, sub, subu, subuswitch, sw, swinc;
  wire [1:0] MemToReg, multiplexer_4_out, multiplexer_5_out, multiplexer_6_out, multiplexer_9_out, RegDist;
  wire [2:0] multiplexer_17_out, op_unit;
  wire [3:0] ALUOp, multiplexer_21_out, multiplexer_23_out, multiplexer_24_out, multiplexer_25_out,
       multiplexer_26_out, multiplexer_27_out, multiplexer_28_out, multiplexer_29_out, multiplexer_30_out,
       multiplexer_31_out, multiplexer_32_out, multiplexer_33_out;
  wire [4:0] RR1, RW;
  wire [5:0] funct;
  wire [15:6] immediate;
  wire [27:0] adder_1_out, bit_extender_4_out;
  wire [31:0] adder_2_out, bit_extender_2_out, bit_extender_3_out, imm, JalAddr, MEM_p8, multiplexer_7_out,
       multiplexer_12_out, multiplexer_13_out, multiplexer_16_out, multiplexer_20_out, overflow, PCin, R, R1,
       R2, shamt, shifter_2_out, SwincOut, WA, X, Y;
  wire [31:16] inst;

  Comparator #(.width(6), .mode("unsigned")) comparator_1 (
    .a(inst[31:26]), .b({6{1'b0}}), .eq(r_type));  // open: gt, lt
  not not_1 (not_1_out, r_type);
  or or_1 (or_1_out, sb, sh, sw, swinc);
  not not_2 (not_2_out, r_type);
  not not_3 (not_3_out, or_2_out);
  or or_2 (or_2_out, j, jal);
  not not_4 (not_4_out, r_type);
  or or_3 (or_3_out, j, jr, jal);
  Comparator #(.width(6), .mode("unsigned")) comparator_2 (.a(funct), .b(6'b100000), .eq(add));  // open: gt, lt
  Comparator #(.width(6), .mode("unsigned")) comparator_3 (.a(inst[31:26]), .b(6'b001000), .eq(addi));  // open: gt, lt
  Comparator #(.width(6), .mode("unsigned")) comparator_4 (.a(inst[31:26]), .b(6'b001001), .eq(addiu));  // open: gt, lt
  Comparator #(.width(6), .mode("unsigned")) comparator_5 (.a(funct), .b(6'b100001), .eq(addu));  // open: gt, lt
  Comparator #(.width(6), .mode("unsigned")) comparator_6 (.a(funct), .b(6'b100100), .eq(\and ));  // open: gt, lt
  Comparator #(.width(6), .mode("unsigned")) comparator_7 (.a(inst[31:26]), .b(6'b001100), .eq(andi));  // open: gt, lt
  Comparator #(.width(6), .mode("unsigned")) comparator_8 (.a(inst[31:26]), .b(6'b000100), .eq(beq));  // open: gt, lt
  assign shamt = {{27{1'b0}}, immediate[10:6]};  // Bit_Extender bit_extender_1
  assign bit_extender_2_out = {{16{immediate[15]}}, {immediate, funct}};  // Bit_Extender bit_extender_2
  assign bit_extender_3_out = {{16{1'b0}}, {immediate, funct}};  // Bit_Extender bit_extender_3
  and and_1 (MemWr, not_1_out, or_1_out);
  and and_2 (ALUSrc, not_2_out, not_3_out);
  and and_3 (Jump, not_4_out, or_3_out);
  Register #(.width(32)) PC (.D(PCin), .Q(FETCH_ADDRESS), .clk(CLOCK));  // open: en, clr
  Register #(.width(32)) LO (.D(R), .en(or_4_out), .Q(LO_Value), .clk(CLOCK));  // open: clr
  Register #(.width(32)) HI (.D(overflow), .en(or_4_out), .Q(HI_Value), .clk(CLOCK));  // open: clr
  or or_4 (or_4_out, multu, divu);
  Multiplexer #(.width(5)) multiplexer_1 (
    .in0(inst[25:21]), .in1(inst[20:16]), .out(RR1), .sel(ShamtSwitch));  // open: en
  Multiplexer #(.width(32)) multiplexer_2 (
    .in0(bit_extender_2_out), .in1(bit_extender_3_out), .out(imm), .sel(ISign));  // open: en
  not not_5 (not_5_out, r_type);
  or or_5 (or_5_out, lbu, lhu, lw, lb);
  not not_6 (not_6_out, r_type);
  or or_6 (or_6_out, beq, beqal, bne);
  Comparator #(.width(6), .mode("unsigned")) comparator_9 (.a(inst[31:26]), .b(6'b010100), .eq(beqal));  // open: gt, lt
  Comparator #(.width(6), .mode("unsigned")) comparator_10 (.a(inst[31:26]), .b(6'b000101), .eq(bne));  // open: gt, lt
  Comparator #(.width(6), .mode("unsigned")) comparator_11 (.a(inst[31:26]), .b(6'b011011), .eq(divu));  // open: gt, lt
  Comparator #(.width(6), .mode("unsigned")) comparator_12 (.a(inst[31:26]), .b(6'b000010), .eq(j));  // open: gt, lt
  Comparator #(.width(6), .mode("unsigned")) comparator_13 (.a(inst[31:26]), .b(6'b000011), .eq(jal));  // open: gt, lt
  Comparator #(.width(6), .mode("unsigned")) comparator_14 (.a(funct), .b(6'b001000), .eq(jr));  // open: gt, lt
  Comparator #(.width(6), .mode("unsigned")) comparator_15 (.a(inst[31:26]), .b(6'b100000), .eq(lb));  // open: gt, lt
  regfile_main main_1 (
    .Read_Register_1(RR1), .Read_Register_2(inst[20:16]), .Write_Register(RW), .Write_Data(WA),
    .Write_Enable(RegWrite), .Clock(CLOCK), .Read_Data_1(R1), .Read_Data_2(R2), .s0_Value(s0_Value),
    .s1_Value(s1_Value), .s2_Value(s2_Value), .ra_Value(ra_Value));
  Multiplexer #(.select(2), .width(5)) multiplexer_3 (
    .in0(inst[20:16]), .in1(immediate[15:11]), .in2({5{1'b1}}), .in3(RR1), .out(RW), .sel(RegDist));  // open: en
  and and_4 (and_4_out, not_5_out, or_5_out);
  and and_5 (and_5_out, r_type, or_7_out);
  or or_7 (or_7_out, sltu, add, addu, \and , sll, slt, sra, srl, subu, sub, mfhi, mflo, \or );
  and and_6 (Branch, not_6_out, or_6_out);
  LED led_1 (.in(main_2_signed_overflow));
  alu_main main_2 (
    .Switch(ALUOp), .X(X), .Equal(equal), .Result(R), .Signed_Overflow(main_2_signed_overflow), .Y(Y),
    .Result_2(overflow));
  assign bit_extender_4_out = {{2{1'b0}}, {inst[25:16], immediate, funct}};  // Bit_Extender bit_extender_4
  Multiplexer #(.width(2)) multiplexer_4 (
    .in0(2'b00), .in1(2'b01), .out(multiplexer_4_out), .sel(and_4_out));  // open: en
  Multiplexer #(.width(2)) multiplexer_5 (
    .in0(multiplexer_4_out), .in1(2'b10), .out(multiplexer_5_out), .sel(or_8_out));  // open: en
  or or_8 (or_8_out, jal, beqal);
  Multiplexer #(.width(2)) multiplexer_6 (
    .in0(2'b00), .in1(2'b01), .out(multiplexer_6_out), .sel(and_5_out));  // open: en
  Comparator #(.width(6), .mode("unsigned")) comparator_16 (.a(inst[31:26]), .b(6'b100100), .eq(lbu));  // open: gt, lt
  Comparator #(.width(6), .mode("unsigned")) comparator_17 (.a(inst[31:26]), .b(6'b100101), .eq(lhu));  // open: gt, lt
  Comparator #(.width(6), .mode("unsigned")) comparator_18 (.a(inst[31:26]), .b(6'b001111), .eq(lui));  // open: gt, lt
  Comparator #(.width(6), .mode("unsigned")) comparator_19 (.a(inst[31:26]), .b(6'b100011), .eq(lw));  // open: gt, lt
  Comparator #(.width(6), .mode("unsigned")) comparator_20 (.a(funct), .b(6'b011001), .eq(multu));  // open: gt, lt
  Comparator #(.width(6), .mode("unsigned")) comparator_21 (.a(funct), .b(6'b010000), .eq(mfhi));  // open: gt, lt
  Comparator #(.width(6), .mode("unsigned")) comparator_22 (.a(funct), .b(6'b010010), .eq(mflo));  // open: gt, lt
  Multiplexer #(.width(32)) multiplexer_7 (.in0(R2), .in1(imm), .out(multiplexer_7_out), .sel(ALUSrc));  // open: en
  Shifter #(.width(28)) shifter_1 (.in(bit_extender_4_out), .\dist (5'b00010), .out(JalAddr[27:0]));
  Adder #(.width(32)) adder_1 (.a(32'h4), .b(FETCH_ADDRESS), .out({JalAddr[31:28], adder_1_out}));  // open: cin, cout
  Shifter #(.width(32)) shifter_2 (.in(imm), .\dist (5'b00010), .out(shifter_2_out));
  Multiplexer #(.width(2)) multiplexer_8 (
    .in0(multiplexer_5_out), .in1(2'b11), .out(MemToReg), .sel(swinc));  // open: en
  Multiplexer #(.width(2)) multiplexer_9 (
    .in0(multiplexer_6_out), .in1(2'b10), .out(multiplexer_9_out), .sel(or_9_out));  // open: en
  or or_9 (or_9_out, jal, beqal);
  not not_7 (not_7_out, r_type);
  or or_10 (or_10_out, andi, ori);
  Multiplexer #(.width(32)) multiplexer_10 (
    .in0(multiplexer_7_out), .in1(shamt), .out(Y), .sel(ShamtSwitch));  // open: en
  Adder #(.width(32)) adder_2 (
    .a({JalAddr[31:28], adder_1_out}), .b(shifter_2_out), .out(adder_2_out));  // open: cin, cout
  Multiplexer #(.width(2)) multiplexer_11 (
    .in0(multiplexer_9_out), .in1(2'b11), .out(RegDist), .sel(swinc));  // open: en
  and and_7 (ISign, not_7_out, or_10_out);
  Comparator #(.width(6), .mode("unsigned")) comparator_23 (.a(funct), .b(6'b100101), .eq(\or ));  // open: gt, lt
  Comparator #(.width(6), .mode("unsigned")) comparator_24 (.a(inst[31:26]), .b(6'b001101), .eq(ori));  // open: gt, lt
  Comparator #(.width(6), .mode("unsigned")) comparator_25 (.a(funct), .b(6'b101010), .eq(slt));  // open: gt, lt
  Comparator #(.width(6), .mode("unsigned")) comparator_26 (.a(inst[31:26]), .b(6'b001010), .eq(slti));  // open: gt, lt
  Comparator #(.width(6), .mode("unsigned")) comparator_27 (.a(funct), .b(6'b101011), .eq(sltu));  // open: gt, lt
  Comparator #(.width(6), .mode("unsigned")) comparator_28 (.a(funct), .b({6{1'b0}}), .eq(sll));  // open: gt, lt
  Comparator #(.width(6), .mode("unsigned")) comparator_29 (.a(funct), .b(6'b000011), .eq(sra));  // open: gt, lt
  // mem_main MEM: pin names not known; wires that end beside it: R, R2, MemWr, MEM_p4, CLOCK, MEM_p6, op_unit, MEM_p8, MEM_p6, MEM_p10, MEM_p10, MEM_p12, MEM_p12, MEM_p14
  Multiplexer #(.width(32)) multiplexer_12 (
    .in0({JalAddr[31:28], adder_1_out}), .in1(adder_2_out), .out(multiplexer_12_out), .sel(PCSrc));  // open: en
  Multiplexer #(.select(2), .width(32)) multiplexer_13 (
    .in0(R), .in1(MEM_p8), .in2(JalAddr), .in3(SwincOut), .out(multiplexer_13_out), .sel(MemToReg));  // open: en
  Multiplexer #(.width(32)) multiplexer_14 (.in0(R1), .in1({32{1'b0}}), .out(X), .sel(lui));  // open: en
  Multiplexer #(.width(32)) multiplexer_15 (
    .in0(multiplexer_12_out), .in1(JalAddr), .out(PCin), .sel(Jump));  // open: en
  or or_11 (or_11_out, beq, beqal);
  not not_8 (not_8_out, equal);
  Multiplexer #(.width(32)) multiplexer_16 (
    .in0(multiplexer_13_out), .in1(HI_Value), .out(multiplexer_16_out), .sel(mfhi));  // open: en
  and and_8 (and_8_out, Branch, equal, or_11_out);
  and and_9 (and_9_out, Branch, not_8_out, bne);
  or or_12 (or_12_out, bne, j, beq, sh, jr, sb, sw);
  Multiplexer #(.width(3)) multiplexer_17 (
    .in0(3'b000), .in1(3'b100), .out(multiplexer_17_out), .sel(swinc));  // open: en
  Comparator #(.width(6), .mode("unsigned")) comparator_30 (.a(funct), .b(6'b000010), .eq(srl));  // open: gt, lt
  Comparator #(.width(6), .mode("unsigned")) comparator_31 (.a(inst[31:26]), .b(6'b101000), .eq(sb));  // open: gt, lt
  Comparator #(.width(6), .mode("unsigned")) comparator_32 (.a(inst[31:26]), .b(6'b101001), .eq(sh));  // open: gt, lt
  Comparator #(.width(6), .mode("unsigned")) comparator_33 (.a(inst[31:26]), .b(6'b101011), .eq(sw));  // open: gt, lt
  Comparator #(.width(6), .mode("unsigned")) comparator_34 (
    .a(inst[31:26]), .b(6'b101100), .eq(swinc));  // open: gt, lt
  Comparator #(.width(6), .mode("unsigned")) comparator_35 (.a(inst[31:26]), .b(6'b100010), .eq(sub));  // open: gt, lt
  Comparator #(.width(6), .mode("unsigned")) comparator_36 (.a(inst[31:26]), .b(6'b100011), .eq(subu));  // open: gt, lt
  Multiplexer #(.width(32)) multiplexer_18 (
    .in0(multiplexer_16_out), .in1(LO_Value), .out(WA), .sel(mflo));  // open: en
  or or_13 (PCSrc, and_8_out, and_9_out);
  and and_10 (and_10_out, ~r_type, or_12_out);  // AND_Gate
  not not_9 (RegWrite, and_10_out);
  Multiplexer #(.select(3), .width(3)) multiplexer_19 (
    .in0(3'b001), .in1(3'b011), .in2(3'b000), .in3(3'b100), .in4(multiplexer_17_out), .in5(3'b010),
    .in6(3'b000), .in7(3'b000), .out(op_unit), .sel(inst[28:26]));  // open: en
  and and_11 (ShamtSwitch, r_type, or_14_out);
  or or_14 (or_14_out, sll, srl, sra);
  or or_15 (or_15_out, Jump, Branch);
  Adder #(.width(32)) adder_3 (.a(R1), .b(32'h4), .out(SwincOut));  // open: cin, cout
  Multiplexer #(.width(32)) multiplexer_20 (
    .in0(INSTRUCTION), .in1({32{1'b0}}), .out(multiplexer_20_out), .sel(or_15_out));  // open: en
  and and_12 (and_12_out, r_type, sll);
  and and_13 (and_13_out, r_type, divu);
  Multiplexer #(.width(4)) multiplexer_21 (
    .in0(multiplexer_32_out), .in1(4'b1000), .out(multiplexer_21_out), .sel(subuswitch));  // open: en
  Multiplexer #(.width(4)) multiplexer_22 (
    .in0(multiplexer_33_out), .in1(4'b1100), .out(ALUOp), .sel(and_14_out));  // open: en
  and and_14 (and_14_out, r_type, sltu);
  Register #(.width(32)) register_1 (
    .D(multiplexer_20_out), .Q({inst, immediate, funct}), .clk(CLOCK));  // open: en, clr
  Multiplexer #(.width(4)) multiplexer_23 (
    .in0(4'b0001), .in1(4'b0000), .out(multiplexer_23_out), .sel(and_12_out));  // open: en
  and and_15 (and_15_out, r_type, srl);
  Multiplexer #(.width(4)) multiplexer_24 (
    .in0(multiplexer_31_out), .in1(4'b0100), .out(multiplexer_24_out), .sel(and_13_out));  // open: en
  Multiplexer #(.width(4)) multiplexer_25 (
    .in0(multiplexer_23_out), .in1(4'b0001), .out(multiplexer_25_out), .sel(and_15_out));  // open: en
  and and_16 (and_16_out, r_type, sra);
  Multiplexer #(.width(4)) multiplexer_26 (
    .in0(multiplexer_24_out), .in1(4'b0101), .out(multiplexer_26_out), .sel(addswitch));  // open: en
  Multiplexer #(.width(4)) multiplexer_27 (
    .in0(multiplexer_21_out), .in1(4'b1001), .out(multiplexer_27_out), .sel(andswitch));  // open: en
  Multiplexer #(.width(4)) multiplexer_28 (
    .in0(multiplexer_25_out), .in1(4'b0010), .out(multiplexer_28_out), .sel(and_16_out));  // open: en
  and and_17 (and_17_out, r_type, multu);
  Multiplexer #(.width(4)) multiplexer_29 (
    .in0(multiplexer_26_out), .in1(4'b0110), .out(multiplexer_29_out), .sel(adduswitch));  // open: en
  Multiplexer #(.width(4)) multiplexer_30 (
    .in0(multiplexer_27_out), .in1(4'b1010), .out(multiplexer_30_out), .sel(orswitch));  // open: en
  Multiplexer #(.width(4)) multiplexer_31 (
    .in0(multiplexer_28_out), .in1(4'b0011), .out(multiplexer_31_out), .sel(and_17_out));  // open: en
  and and_18 (and_18_out, r_type, sub);
  Multiplexer #(.width(4)) multiplexer_32 (
    .in0(multiplexer_29_out), .in1(4'b0111), .out(multiplexer_32_out), .sel(and_18_out));  // open: en
  Multiplexer #(.width(4)) multiplexer_33 (
    .in0(multiplexer_30_out), .in1(4'b1011), .out(multiplexer_33_out), .sel(sltswitch));  // open: en
  not not_10 (not_10_out, r_type);
  not not_11 (not_11_out, r_type);
  not not_12 (not_12_out, r_type);
  not not_13 (not_13_out, r_type);
  or or_16 (or_16_out, beq, beqal, bne);
  not not_14 (not_14_out, r_type);
  and and_19 (and_19_out, addi, not_10_out);
  and and_20 (and_20_out, andi, not_11_out);
  and and_21 (and_21_out, slti, not_12_out);
  and and_22 (and_22_out, ori, not_13_out);
  and and_23 (and_23_out, or_16_out, not_14_out);
  or or_17 (addswitch, add, and_19_out);
  or or_18 (or_18_out, addiu, lb, lbu, lhu, lui, lw, sb, sh, sw, swinc);
  not not_15 (not_15_out, r_type);
  or or_19 (andswitch, \and , and_20_out);
  or or_20 (sltswitch, slt, and_21_out);
  or or_21 (orswitch, \or , and_22_out);
  or or_22 (subuswitch, subu, and_23_out);
  and and_24 (and_24_out, or_18_out, not_15_out);
  or or_23 (adduswitch, addu, and_24_out);

  // Other names for the same wires on the sheet: clk = CLOCK; fetch_addr[31:0] = FETCH_ADDRESS;
  //   PCout[31:0] = FETCH_ADDRESS; HI[31:0] = HI_Value; immediate[5:0] = funct; inst[15:0] = {immediate, funct};
  //   RR2[4:0] = inst[20:16]; opcode[5:0] = inst[31:26]; LO[31:0] = LO_Value; ra[31:0] = ra_Value;
  //   s0[31:0] = s0_Value; s1[31:0] = s1_Value; s2[31:0] = s2_Value

  // Notes on the sheet:
  //   Datapath
  //   Control
  //   2. Instruction Decode
  //   MemWr
  //   ALUSrc
  //   Jump
  //   Output
  //   R types
  //   These are outputs/inputs from run.circ
  //   Inputs
  //   J - Type
  //   RegDist
  //   Branch
  //   MemToReg
  //   1. Instruction Fetch
  //   ISign
  //   3. Execute
  //   These are DEBUG/TEST outputs from your circuit.
  //   RegWrite
  //   PCSrc
  //   OPUnit
  //   Pipelining
  //   ALUOp
endmodule
