// Logisim project cpu_FINAL.circ as structural Verilog: 4 circuits, main circuit main
module main (
  input  [31:0] INSTRUCTION,
  input  CLOCK,
  output [31:0] FETCH_ADDRESS,
  output [31:0] s0_Value,
  output [31:0] s1_Value,
  output [31:0] s2_Value,
  output [31:0] ra_Value,
  output [31:0] HI_Value,
  output [31:0] LO_Value
);

  wire ALUSrc, and_2_out, beq, beqal, beqal_mux, bne, divu, equal, ExtOp, j, jal, Jr, Jump, jump_inst, kill,
       lui, main_2_signed_overflow, MemRead, MemToReg, MemWrite, mfhi, mflo, multu, multu_or_divu, mux_ctrl,
       not_1_out, or_2_out, or_6_out, RegDest, RegWrite, shift_inst, swinc;
  wire [2:0] OP_Unit;
  wire [3:0] ALUCtrl;
  wire [4:0] multiplexer_5_out, multiplexer_6_out, multiplexer_7_out, multiplexer_8_out, rd, rs, rt, shamt;
  wire [5:0] funct, opcode;
  wire [15:0] immediate;
  wire [25:0] addr;
  wire [27:0] bit_extender_1_out, shifter_1_out;
  wire [31:0] adder_2_out, adder_3_out, bit_extender_2_out, bit_extender_3_out, cPC, extender_1_output,
       INSTRUCTION_t, jr_address, main_2_result, main_2_result_2, MEM_p6, multiplexer_2_out,
       multiplexer_3_out, multiplexer_4_out, multiplexer_9_out, multiplexer_10_out, multiplexer_11_out,
       multiplexer_12_out, multiplexer_13_out, multiplexer_14_out, multiplexer_15_out, shifter_2_out,
       shifter_3_out, W_Mem, write_back;

  Control control_1 (
    .in_1(INSTRUCTION_t), .j(j), .jal(jal), .Jr(Jr), .beq(beq), .bne(bne), .beqal(beqal),
    .MemWrite(MemWrite), .MemToReg(MemToReg), .RegWrite(RegWrite), .ALUSrc(ALUSrc), .MemRead(MemRead),
    .ExtOP(ExtOp), .lui(lui), .Jump(Jump), .OPUnit(OP_Unit), .mflo(mflo), .mfhi(mfhi), .RegDest(RegDest),
    .ALUCtrl(ALUCtrl), .shamt(shamt), .rd(rd), .funct(funct), .rt(rt), .rs(rs), .opcode(opcode),
    .imm(immediate), .addr(addr), .multu(multu), .divu(divu), .shift_inst(shift_inst), .swinc(swinc));
  assign bit_extender_1_out = {{2{1'b0}}, addr};  // Bit_Extender bit_extender_1
  assign bit_extender_2_out = {{16{immediate[15]}}, immediate};  // Bit_Extender bit_extender_2
  Shifter #(.width(28)) shifter_1 (.in(bit_extender_1_out), .\dist (5'b00010), .out(shifter_1_out));
  Shifter #(.width(32)) shifter_2 (.in(bit_extender_2_out), .\dist (5'b00010), .out(shifter_2_out));
  Multiplexer #(.width(32)) multiplexer_1 (.in1({32{1'b0}}), .out(INSTRUCTION), .sel(kill));  // open: in0, en
  Register #(.width(32)) pipeline (.D(INSTRUCTION), .Q(INSTRUCTION_t), .clk(CLOCK));  // open: en, clr
  Adder #(.width(32)) adder_1 (.a(32'h4), .b(FETCH_ADDRESS), .out(cPC));  // open: cin, cout
  Adder #(.width(32)) adder_2 (.a(cPC), .b(shifter_2_out), .out(adder_2_out));  // open: cin, cout
  or or_1 (jump_inst, jal, j);
  or or_2 (or_2_out, beqal, beq);
  not not_1 (not_1_out, equal);
  Multiplexer #(.width(32)) multiplexer_2 (
    .in0(cPC), .in1(adder_2_out), .out(multiplexer_2_out), .sel(mux_ctrl));  // open: en
  and and_1 (beqal_mux, equal, or_2_out);
  and and_2 (and_2_out, not_1_out, bne);
  or or_3 (multu_or_divu, multu, divu);
  Multiplexer #(.width(32)) multiplexer_3 (
    .in0(multiplexer_2_out), .in1({cPC[31:28], shifter_1_out}), .out(multiplexer_3_out), .sel(jump_inst));  // open: en
  or or_4 (mux_ctrl, beqal_mux, and_2_out);
  Multiplexer #(.width(32)) multiplexer_4 (
    .in0(multiplexer_3_out), .in1(jr_address), .out(multiplexer_4_out), .sel(Jr));  // open: en
  Register #(.width(32)) PC (.D(multiplexer_4_out), .Q(FETCH_ADDRESS), .clk(CLOCK));  // open: en, clr
  or or_5 (kill, jump_inst, beqal, beq, bne, Jr);
  Multiplexer #(.width(5)) multiplexer_5 (.in0(rt), .in1(rd), .out(multiplexer_5_out), .sel(RegDest));  // open: en
  Multiplexer #(.width(5)) multiplexer_6 (
    .in0(multiplexer_5_out), .in1(rs), .out(multiplexer_6_out), .sel(swinc));  // open: en
  or or_6 (or_6_out, jal, beqal_mux);
  Multiplexer #(.width(5)) multiplexer_7 (.in0(rs), .in1(rt), .out(multiplexer_7_out), .sel(shift_inst));  // open: en
  Multiplexer #(.width(5)) multiplexer_8 (
    .in0(multiplexer_6_out), .in1({5{1'b1}}), .out(multiplexer_8_out), .sel(or_6_out));  // open: en
  regfile_main main_1 (
    .Read_Register_1(multiplexer_7_out), .Read_Register_2(rt), .Write_Register(multiplexer_8_out),
    .Write_Data(write_back), .Write_Enable(RegWrite), .Clock(CLOCK), .Read_Data_1(jr_address),
    .Read_Data_2(W_Mem), .s0_Value(s0_Value), .s1_Value(s1_Value), .s2_Value(s2_Value), .ra_Value(ra_Value));
  Extender extender_1 (.in(immediate), .ExtOP(ExtOp), .\output (extender_1_output));
  Multiplexer #(.width(32)) multiplexer_9 (
    .in0(W_Mem), .in1(extender_1_output), .out(multiplexer_9_out), .sel(ALUSrc));  // open: en
  Multiplexer #(.width(32)) multiplexer_10 (
    .in0(multiplexer_9_out), .in1(shifter_3_out), .out(multiplexer_10_out), .sel(lui));  // open: en
  Shifter #(.width(32)) shifter_3 (.in(multiplexer_9_out), .\dist (5'b10000), .out(shifter_3_out));
  assign bit_extender_3_out = {{27{1'b0}}, shamt};  // Bit_Extender bit_extender_3
  LED led_1 (.in(main_2_signed_overflow));
  alu_main main_2 (
    .Switch(ALUCtrl), .X(jr_address), .Equal(equal), .Result(main_2_result),
    .Signed_Overflow(main_2_signed_overflow), .Y(multiplexer_11_out), .Result_2(main_2_result_2));
  Multiplexer #(.width(32)) multiplexer_11 (
    .in0(multiplexer_10_out), .in1(bit_extender_3_out), .out(multiplexer_11_out), .sel(shift_inst));  // open: en
  Register #(.width(32)) HI (.D(main_2_result_2), .en(multu_or_divu), .Q(HI_Value), .clk(CLOCK));  // open: clr
  Register #(.width(32)) LO (.D(main_2_result), .en(multu_or_divu), .Q(LO_Value), .clk(CLOCK));  // open: clr
  // mem_main MEM: pin names not known; wires that end beside it: main_2_result, W_Mem, MemWrite, CLOCK, OP_Unit, MEM_p6
  Multiplexer #(.width(32)) multiplexer_12 (
    .in0(main_2_result), .in1(MEM_p6), .out(multiplexer_12_out), .sel(MemToReg));  // open: en
  Multiplexer #(.width(32)) multiplexer_13 (
    .in0(multiplexer_12_out), .in1(cPC), .out(multiplexer_13_out), .sel(jal));  // open: en
  Multiplexer #(.width(32)) multiplexer_14 (
    .in0(multiplexer_13_out), .in1(HI_Value), .out(multiplexer_14_out), .sel(mfhi));  // open: en
  Multiplexer #(.width(32)) multiplexer_15 (
    .in0(multiplexer_14_out), .in1(LO_Value), .out(multiplexer_15_out), .sel(mflo));  // open: en
  Adder #(.width(32)) adder_3 (.a(jr_address), .b(32'h4), .out(adder_3_out));  // open: cin, cout
  Multiplexer #(.width(32)) multiplexer_16 (
    .in0(multiplexer_15_out), .in1(adder_3_out), .out(write_back), .sel(swinc));  // open: en

  // Other names for the same wires on the sheet: clk = CLOCK; fetch_addr[31:0] = FETCH_ADDRESS; hi[31:0] = HI_Value;
  //   lo[31:0] = LO_Value; ra[31:0] = ra_Value; s0[31:0] = s0_Value; s1[31:0] = s1_Value; s2[31:0] = s2_Value;
  //   swinckr[31:0] = jr_address

  // Notes on the sheet:
  //   Output
  //   These are outputs/inputs from run.circ
  //   Inputs
  //   mux for jump
  //   These are DEBUG/TEST outputs from your circuit.
endmodule

module Control (
  input  [31:0] in_1,
  output swinc,
  output shift_inst,
  output RegDest,
  output Jump,
  output MemToReg,
  output MemRead,
  output j,
  output ALUSrc,
  output MemWrite,
  output jal,
  output Jr,
  output RegWrite,
  output beq,
  output bne,
  output ExtOP,
  output beqal,
  output [2:0] OPUnit,
  output lui,
  output [3:0] ALUCtrl,
  output mfhi,
  output multu,
  output divu,
  output mflo,
  output [25:0] addr,
  output [15:0] imm,
  output [4:0] rs,
  output [4:0] rd,
  output [4:0] rt,
  output [5:0] opcode,
  output [4:0] shamt,
  output [5:0] funct
);

  wire add, addi, addiu, addu, \and , and_17_out, andi, comparator_1_eq, comparator_2_eq, comparator_3_eq,
       comparator_4_eq, comparator_5_eq, comparator_6_eq, comparator_7_eq, comparator_8_eq, comparator_9_eq,
       comparator_10_eq, comparator_18_eq, comparator_19_eq, comparator_20_eq, comparator_21_eq,
       comparator_22_eq, comparator_23_eq, comparator_24_eq, lb, lbu, lhu, lw, not_1_out, not_2_out,
       not_3_out, not_4_out, \or , or_9_out, or_14_out, ori, R_Type, sb, sh, sll, slt, slti, sltu, sra, srl,
       sub, subu, sw, switch5, switch6, switch7, switch9, switch10, switch11;
  wire [2:0] multiplexer_1_out;
  wire [3:0] bit_extender_1_out, bit_extender_2_out, bit_extender_3_out, bit_extender_4_out,
       bit_extender_5_out, bit_extender_6_out, bit_extender_7_out, bit_extender_8_out, bit_extender_9_out,
       bit_extender_10_out, bit_extender_11_out, bit_extender_12_out, bit_extender_13_out, val0, val1, val2,
       val3, val4, val5, val6, val7, val8, val9, val10, val11, val12;

  Comparator #(.width(6)) comparator_1 (.a(in_1[5:0]), .b(6'b001000), .eq(comparator_1_eq));  // open: gt, lt
  Comparator #(.width(6)) comparator_2 (.a(in_1[31:26]), .b({6{1'b0}}), .eq(comparator_2_eq));  // open: gt, lt
  Comparator #(.width(6)) comparator_3 (.a(in_1[5:0]), .b(6'b100011), .eq(comparator_3_eq));  // open: gt, lt
  Comparator #(.width(6)) comparator_4 (.a(in_1[5:0]), .b(6'b100010), .eq(comparator_4_eq));  // open: gt, lt
  Comparator #(.width(6)) comparator_5 (.a(in_1[5:0]), .b(6'b000011), .eq(comparator_5_eq));  // open: gt, lt
  Comparator #(.width(6)) comparator_6 (.a(in_1[5:0]), .b(6'b010000), .eq(comparator_6_eq));  // open: gt, lt
  Comparator #(.width(6)) comparator_7 (.a(in_1[5:0]), .b(6'b011001), .eq(comparator_7_eq));  // open: gt, lt
  Comparator #(.width(6)) comparator_8 (.a(in_1[5:0]), .b(6'b011011), .eq(comparator_8_eq));  // open: gt, lt
  Comparator #(.width(6)) comparator_9 (.a(in_1[5:0]), .b(6'b010010), .eq(comparator_9_eq));  // open: gt, lt
  Comparator #(.width(6)) comparator_10 (.a(in_1[5:0]), .b(6'b000010), .eq(comparator_10_eq));  // open: gt, lt
  Comparator #(.width(6)) comparator_11 (.a(in_1[31:26]), .b(6'b000010), .eq(j));  // open: gt, lt
  Comparator #(.width(6)) comparator_12 (.a(in_1[31:26]), .b(6'b000011), .eq(jal));  // open: gt, lt
  and and_1 (Jr, comparator_1_eq, comparator_2_eq);
  Comparator #(.width(6)) comparator_13 (.a(in_1[31:26]), .b(6'b000100), .eq(beq));  // open: gt, lt
  Comparator #(.width(6)) comparator_14 (.a(in_1[31:26]), .b(6'b000101), .eq(bne));  // open: gt, lt
  Comparator #(.width(6)) comparator_15 (.a(in_1[31:26]), .b(6'b010100), .eq(beqal));  // open: gt, lt
  Comparator #(.width(6)) comparator_16 (.a(in_1[31:26]), .b(6'b001111), .eq(lui));  // open: gt, lt
  Comparator #(.width(6)) comparator_17 (.a(in_1[31:26]), .b({6{1'b0}}), .eq(R_Type));  // open: gt, lt
  and and_2 (subu, R_Type, comparator_3_eq);
  and and_3 (sub, R_Type, comparator_4_eq);
  and and_4 (sra, R_Type, comparator_5_eq);
  and and_5 (mfhi, R_Type, comparator_6_eq);
  and and_6 (multu, R_Type, comparator_7_eq);
  and and_7 (divu, R_Type, comparator_8_eq);
  and and_8 (mflo, R_Type, comparator_9_eq);
  and and_9 (srl, R_Type, comparator_10_eq);
  Comparator #(.width(6)) comparator_18 (.a(in_1[5:0]), .b(6'b100000), .eq(comparator_18_eq));  // open: gt, lt
  Comparator #(.width(6)) comparator_19 (.a(in_1[5:0]), .b(6'b100001), .eq(comparator_19_eq));  // open: gt, lt
  Comparator #(.width(6)) comparator_20 (.a(in_1[5:0]), .b(6'b100100), .eq(comparator_20_eq));  // open: gt, lt
  Comparator #(.width(6)) comparator_21 (.a(in_1[5:0]), .b(6'b100101), .eq(comparator_21_eq));  // open: gt, lt
  Comparator #(.width(6)) comparator_22 (.a(in_1[5:0]), .b(6'b101010), .eq(comparator_22_eq));  // open: gt, lt
  Comparator #(.width(6)) comparator_23 (.a(in_1[5:0]), .b(6'b101011), .eq(comparator_23_eq));  // open: gt, lt
  Comparator #(.width(6)) comparator_24 (.a(in_1[5:0]), .b({6{1'b0}}), .eq(comparator_24_eq));  // open: gt, lt
  Multiplexer #(.width(3)) multiplexer_1 (
    .in0(3'b000), .in1(3'b100), .out(multiplexer_1_out), .sel(swinc));  // open: en
  and and_10 (add, R_Type, comparator_18_eq);
  and and_11 (addu, R_Type, comparator_19_eq);
  and and_12 (\and , R_Type, comparator_20_eq);
  and and_13 (\or , R_Type, comparator_21_eq);
  and and_14 (slt, R_Type, comparator_22_eq);
  and and_15 (sltu, R_Type, comparator_23_eq);
  and and_16 (sll, R_Type, comparator_24_eq);
  or or_1 (Jump, jal, j, Jr);
  or or_2 (MemRead, lb, lbu, lw, lhu);
  or or_3 (MemWrite, sw, sh, sb, swinc);
  or or_4 (ExtOP, swinc, addi, addiu, lbu, lhu, lw, sw, slti, sb, sh, lb);
  Multiplexer #(.select(3), .width(3)) multiplexer_2 (
    .in0(3'b000), .in1(3'b011), .in3(3'b100), .in4(multiplexer_1_out), .in5(3'b010), .out(OPUnit),
    .sel(in_1[28:26]));  // open: in2, in6, in7, en
  Comparator #(.width(6)) comparator_25 (.a(in_1[31:26]), .b(6'b001000), .eq(addi));  // open: gt, lt
  Comparator #(.width(6)) comparator_26 (.a(in_1[31:26]), .b(6'b001001), .eq(addiu));  // open: gt, lt
  Comparator #(.width(6)) comparator_27 (.a(in_1[31:26]), .b(6'b001100), .eq(andi));  // open: gt, lt
  Comparator #(.width(6)) comparator_28 (.a(in_1[31:26]), .b(6'b100100), .eq(lbu));  // open: gt, lt
  Comparator #(.width(6)) comparator_29 (.a(in_1[31:26]), .b(6'b100101), .eq(lhu));  // open: gt, lt
  Comparator #(.width(6)) comparator_30 (.a(in_1[31:26]), .b(6'b001010), .eq(slti));  // open: gt, lt
  Comparator #(.width(6)) comparator_31 (.a(in_1[31:26]), .b(6'b100000), .eq(lb));  // open: gt, lt
  Comparator #(.width(6)) comparator_32 (.a(in_1[31:26]), .b(6'b001101), .eq(ori));  // open: gt, lt
  Comparator #(.width(6)) comparator_33 (.a(in_1[31:26]), .b(6'b101000), .eq(sb));  // open: gt, lt
  Comparator #(.width(6)) comparator_34 (.a(in_1[31:26]), .b(6'b101001), .eq(sh));  // open: gt, lt
  Comparator #(.width(6)) comparator_35 (.a(in_1[31:26]), .b(6'b101011), .eq(sw));  // open: gt, lt
  Comparator #(.width(6)) comparator_36 (.a(in_1[31:26]), .b(6'b100011), .eq(lw));  // open: gt, lt
  Comparator #(.width(6)) comparator_37 (.a(in_1[31:26]), .b(6'b101100), .eq(swinc));  // open: gt, lt
  not not_1 (not_1_out, multu);
  not not_2 (not_2_out, multu);
  not not_3 (not_3_out, divu);
  not not_4 (not_4_out, divu);
  and and_17 (and_17_out, R_Type, not_2_out, not_3_out);
  or or_5 (switch7, sub, beq, bne, beqal);
  or or_6 (switch9, andi, \and );
  or or_7 (switch10, ori, \or );
  or or_8 (switch11, slt, slti);
  and and_18 (RegDest, not_1_out, not_4_out, R_Type);
  or or_9 (or_9_out, jal, lbu, lhu, lw, lb);
  or or_10 (switch5, add, addi);
  or or_11 (switch6, lb, lw, lui, addu, lbu, swinc, lhu, addiu, sb, sh, sw);
  or or_12 (RegWrite, beqal, andi, and_17_out, addi, addiu, lui, ori, slti, swinc, or_9_out);
  assign bit_extender_1_out = {{3{srl}}, srl};  // Bit_Extender bit_extender_1
  assign bit_extender_2_out = {{3{sra}}, sra};  // Bit_Extender bit_extender_2
  assign bit_extender_3_out = {{3{multu}}, multu};  // Bit_Extender bit_extender_3
  assign bit_extender_4_out = {{3{divu}}, divu};  // Bit_Extender bit_extender_4
  assign bit_extender_5_out = {{3{switch5}}, switch5};  // Bit_Extender bit_extender_5
  assign bit_extender_6_out = {{3{switch6}}, switch6};  // Bit_Extender bit_extender_6
  assign bit_extender_7_out = {{3{switch7}}, switch7};  // Bit_Extender bit_extender_7
  assign bit_extender_8_out = {{3{subu}}, subu};  // Bit_Extender bit_extender_8
  assign bit_extender_9_out = {{3{switch9}}, switch9};  // Bit_Extender bit_extender_9
  assign bit_extender_10_out = {{3{switch10}}, switch10};  // Bit_Extender bit_extender_10
  assign bit_extender_11_out = {{3{switch11}}, switch11};  // Bit_Extender bit_extender_11
  assign bit_extender_12_out = {{3{sltu}}, sltu};  // Bit_Extender bit_extender_12
  or or_13 (shift_inst, sll, srl, sra);
  assign bit_extender_13_out = {{3{sll}}, sll};  // Bit_Extender bit_extender_13
  assign val0 = bit_extender_13_out & 4'b0000;  // AND_Gate and_19, 4 bits wide
  assign val1 = bit_extender_1_out & 4'b0001;  // AND_Gate and_20, 4 bits wide
  assign val2 = bit_extender_2_out & 4'b0010;  // AND_Gate and_21, 4 bits wide
  assign val3 = bit_extender_3_out & 4'b0011;  // AND_Gate and_22, 4 bits wide
  assign val4 = bit_extender_4_out & 4'b0100;  // AND_Gate and_23, 4 bits wide
  assign val5 = bit_extender_5_out & 4'b0101;  // AND_Gate and_24, 4 bits wide
  assign val6 = bit_extender_6_out & 4'b0110;  // AND_Gate and_25, 4 bits wide
  assign val7 = bit_extender_7_out & 4'b0111;  // AND_Gate and_26, 4 bits wide
  assign val8 = bit_extender_8_out & 4'b1000;  // AND_Gate and_27, 4 bits wide
  assign val9 = bit_extender_9_out & 4'b1001;  // AND_Gate and_28, 4 bits wide
  assign val10 = bit_extender_10_out & 4'b1010;  // AND_Gate and_29, 4 bits wide
  assign val11 = bit_extender_11_out & 4'b1011;  // AND_Gate and_30, 4 bits wide
  assign val12 = bit_extender_12_out & 4'b1100;  // AND_Gate and_31, 4 bits wide
  or or_14 (or_14_out, lbu, lhu, lw, lb);
  or or_15 (ALUSrc, sb, sw, addi, addiu, swinc, lui, ori, slti, andi, or_14_out);
  assign ALUCtrl = val0 | val1 | val2 | val3 | val4 | val5 | val6 | val7 | val8 | val9 | val10 | val11 | val12;  // OR_Gate or_16, 4 bits wide

  assign addr = in_1[25:0];
  assign funct = in_1[5:0];
  assign imm = in_1[15:0];
  assign MemToReg = MemRead;
  assign opcode = in_1[31:26];
  assign rd = in_1[15:11];
  assign rs = in_1[25:21];
  assign rt = in_1[20:16];
  assign shamt = in_1[10:6];

  // Other names for the same wires on the sheet: immediate[15:0] = in_1[15:0]; is_memRead = MemRead;
  //   is_memWrite = MemWrite; switch0 = sll; switch1 = srl; switch2 = sra; switch3 = multu; switch4 = divu;
  //   switch8 = subu; switch12 = sltu

  // Notes on the sheet:
  //   Dont forget swinc bitch :)
  //   beqal rs rt label
  //   if rs = rt:
  //   r[31] = PC
  //   else:
  //   PC = PC + 4 + BranchAddr
  //   AluSrc controls a mux that determines whether second operand in ALU is a register or an immediate
  //   swinc rt offset(rs)
  //   mem[rs + imm] = rt
  //   rs = rs + imm
endmodule

module Decoder (
  input  [25:0] addr,
  input  [31:0] in_2,
  input  [5:0] funct,
  input  [4:0] shamt,
  input  [4:0] rd,
  input  [4:0] rs,
  input  [4:0] rt,
  input  [5:0] opcode,
  input  [15:0] imm
);


  assign funct = addr[5:0];
  assign imm = addr[15:0];
  assign in_2[25:0] = addr;
  assign opcode = in_2[31:26];
  assign rd = addr[15:11];
  assign rs = addr[20:16];
  assign rt = addr[25:21];
  assign shamt = addr[10:6];

  // Other names for the same wires on the sheet: immediate[15:0] = addr[15:0]; rt_t[4:0] = addr[20:16];
  //   rs_t[4:0] = addr[25:21]
endmodule

module Extender (
  input  [15:0] in,
  input  ExtOP,
  output [31:0] \output 
);

  wire [31:0] bit_extender_1_out, bit_extender_2_out;

  assign bit_extender_1_out = {{16{1'b0}}, in};  // Bit_Extender bit_extender_1
  assign bit_extender_2_out = {{16{in[15]}}, in};  // Bit_Extender bit_extender_2
  Multiplexer #(.width(32)) multiplexer_1 (
    .in0(bit_extender_1_out), .in1(bit_extender_2_out), .out(\output ), .sel(ExtOP));  // open: en
endmodule
