// Logisim project alu.circ as structural Verilog: 1 circuit, main circuit main
module main (
  input  [31:0] X,
  input  [31:0] Y,
  input  [3:0] Switch,
  output Signed_Overflow,
  output Equal,
  output [31:0] Result,
  output [31:0] Result_2
);

  wire and_2_out, comparator_2_eq, comparator_4_eq, comparator_5_eq, comparator_6_lt, comparator_7_lt,
       comparator_8_gt, comparator_8_lt, comparator_9_eq, multiplexer_1_out, multiplexer_4_out,
       multiplexer_5_out, not_1_out, not_2_out, or_3_out, overflow1, overflow_2, rBitS;
  wire [30:0] sub;
  wire [31:0] add, addu, \and , div_ret, divu, mul_ret, multu, \or , sll, slt, sltu, sra, srl, subu;

  assign \and  = X & Y;  // AND_Gate and_1, 32 bits wide
  assign \or  = X | Y;  // OR_Gate or_1, 32 bits wide
  Adder #(.width(32)) adder_1 (.a(X), .b(Y), .out(addu));  // open: cin, cout
  Multiplier #(.width(32)) multiplier_1 (.a(X), .b(Y), .out(multu), .cout(mul_ret));  // open: cin
  Divider #(.width(32)) divider_1 (.a(X), .b(Y), .out(divu), .rem(div_ret));  // open: upper
  Subtractor #(.width(32)) subtractor_1 (.a(X), .b(Y), .out(subu));  // open: bin, bout
  Comparator #(.width(32)) comparator_1 (.a(X), .b(Y), .eq(Equal));  // open: gt, lt
  Comparator #(.width(1)) comparator_2 (.a(X[31]), .b(Y[31]), .eq(comparator_2_eq));  // open: gt, lt
  Adder #(.width(32)) adder_2 (.a(X), .b(Y), .out(add));  // open: cin, cout
  not not_1 (not_1_out, add[31]);
  Multiplexer multiplexer_1 (.in0(add[31]), .in1(X[31]), .out(multiplexer_1_out), .sel(comparator_2_eq));  // open: en
  Multiplexer #(.select(4), .width(32)) multiplexer_2 (
    .in0({32{1'b0}}), .in1({32{1'b0}}), .in2({32{1'b0}}), .in3(mul_ret), .in4(div_ret), .in5({32{1'b0}}),
    .in6({32{1'b0}}), .in7({32{1'b0}}), .in8({32{1'b0}}), .in9({32{1'b0}}), .in10({32{1'b0}}),
    .in11({32{1'b0}}), .in12({32{1'b0}}), .in13({32{1'b0}}), .in14({32{1'b0}}), .in15({32{1'b0}}),
    .out(Result_2), .sel(Switch));  // open: en
  Multiplexer #(.select(4), .width(32)) multiplexer_3 (
    .in0(sll), .in1(srl), .in2(sra), .in3(multu), .in4(divu), .in5(add), .in6(addu), .in7({rBitS, sub}),
    .in8(subu), .in9(\and ), .in10(\or ), .in11(slt), .in12(sltu), .in13({32{1'b0}}), .in14({32{1'b0}}),
    .in15({32{1'b0}}), .out(Result), .sel(Switch));  // open: en
  Comparator #(.width(1)) comparator_3 (.a(not_1_out), .b(multiplexer_1_out), .eq(overflow1));  // open: gt, lt
  Comparator #(.width(4)) comparator_4 (.a(4'b0111), .b(Switch), .eq(comparator_4_eq));  // open: gt, lt
  Comparator #(.width(4)) comparator_5 (.a(Switch), .b(4'b0101), .eq(comparator_5_eq));  // open: gt, lt
  Multiplexer multiplexer_4 (.in0(1'b0), .in1(overflow_2), .out(multiplexer_4_out), .sel(comparator_4_eq));  // open: en
  or or_2 (Signed_Overflow, multiplexer_4_out, multiplexer_5_out);
  Multiplexer multiplexer_5 (.in0(1'b0), .in1(overflow1), .out(multiplexer_5_out), .sel(comparator_5_eq));  // open: en
  Comparator #(.width(32)) comparator_6 (.a(X), .b(Y), .lt(comparator_6_lt));  // open: gt, eq
  Comparator #(.width(32), .mode("unsigned")) comparator_7 (.a(X), .b(Y), .lt(comparator_7_lt));  // open: gt, eq
  assign slt = {{31{1'b0}}, comparator_6_lt};  // Bit_Extender bit_extender_1
  assign sltu = {{31{1'b0}}, comparator_7_lt};  // Bit_Extender bit_extender_2
  Subtractor #(.width(32)) subtractor_2 (.a(X), .b(Y), .out({rBitS, sub}));  // open: bin, bout
  Comparator #(.width(1)) comparator_8 (.a(rBitS), .b(X[31]), .gt(comparator_8_gt), .lt(comparator_8_lt));  // open: eq
  not not_2 (not_2_out, Y[31]);
  or or_3 (or_3_out, comparator_8_gt, comparator_8_lt);
  and and_2 (and_2_out, or_3_out, comparator_9_eq);
  Comparator #(.width(1)) comparator_9 (.a(X[31]), .b(not_2_out), .eq(comparator_9_eq));  // open: gt, lt
  Multiplexer multiplexer_6 (.in0(1'b0), .in1(1'b1), .out(overflow_2), .sel(and_2_out));  // open: en
  Shifter #(.width(32)) shifter_1 (.in(X), .\dist (Y[4:0]), .out(sll));
  Shifter #(.width(32), .shift("lr")) shifter_2 (.in(X), .\dist (Y[4:0]), .out(srl));
  // Probe on sra
  Shifter #(.width(32), .shift("ar")) shifter_3 (.in(X), .\dist (Y[4:0]), .out(sra));

  // Other names for the same wires on the sheet: rBit = add[31]; overflow = Signed_Overflow; S[3:0] = Switch;
  //   sub[31] = rBitS; xBit = X[31]; xBitS = X[31]; yBit = Y[31]; yBitS = Y[31]

  // Notes on the sheet:
  //   INPUTS to your circuit
  //   DON'T CHANGE THE LOCATIONS OF THE INPUTS AND OUTPUTS!
  //   OUTPUTS from your circuit
  //   *** shifts ***
endmodule
