// Logisim project cpu.circ as structural Verilog: 2 circuits, main circuit main
module main (
  input  [31:0] INSTRUCTION,
  input  CLOCK,
  output [31:0] FETCH_ADDRESS,
  output [31:0] s0_Value,
  output [31:0] s1_Value,
  output [31:0] s2_Value,
  output [31:0] ra_Value,
  output [31:0] HI_Value,
  output [31:0] LO_Value
);

  wire ALUSrc, and_2_out, and_3_out, and_7_out, Branch, eq, hi_logic, Jr, Jump, Link, lo_logic, Lui,
       main_2_signed_overflow, MemRead, MemtoReg, MemWrite, mf_logic, nand_1_out, nop, not_1_out, or_1_out,
       RegDst, RegWrite, RType, sh, shift_logic, sign_logic, Swinc, write_mf;
  wire [2:0] OPUnit;
  wire [3:0] ALUCtr;
  wire [4:0] multiplexer_1_out, multiplexer_4_out, multiplexer_6_out, multiplexer_8_out;
  wire [5:0] func, op_code;
  wire [27:0] PC_4;
  wire [31:0] adder_2_out, alu_out1, alu_out2, bit_extender_1_out, bit_extender_2_out, bit_extender_3_out,
       data, imm, mem_out, multiplexer_2_out, multiplexer_5_out, multiplexer_7_out, multiplexer_9_out,
       multiplexer_12_out, multiplexer_13_out, multiplexer_14_out, multiplexer_15_out, multiplexer_16_out,
       next_pc, register_1_q, rs_data, rt_data, shifter_1_out, shifter_2_out;
  wire [31:8] jump_addr;

  Register #(.width(32)) register_1 (.D(INSTRUCTION), .Q(register_1_q), .clk(CLOCK));  // open: en, clr
  or or_1 (or_1_out, Jr, Jump, Branch);
  Multiplexer #(.width(5), .enable("false")) multiplexer_1 (
    .in0(jump_addr[22:18]), .in1(jump_addr[17:13]), .out(multiplexer_1_out), .sel(RegDst));
  Multiplexer #(.width(32), .enable("false")) multiplexer_2 (
    .in0(HI_Value), .in1(LO_Value), .out(multiplexer_2_out), .sel(mf_logic));
  Multiplexer #(.width(32), .enable("false")) multiplexer_3 (
    .in0(register_1_q), .in1({32{1'b0}}), .out({op_code, jump_addr[27:8], func}), .sel(nop));
  Register #(.width(1)) register_2 (.D(or_1_out), .Q(nop), .clk(CLOCK));  // open: en, clr
  Multiplexer #(.width(5), .enable("false")) multiplexer_4 (
    .in0(multiplexer_1_out), .in1({5{1'b1}}), .out(multiplexer_4_out), .sel(Link));
  Register #(.width(32)) PC (.D(multiplexer_5_out), .Q(FETCH_ADDRESS), .clk(CLOCK));  // open: en, clr
  Multiplexer #(.width(32), .enable("false")) multiplexer_5 (
    .in0(next_pc), .in1(FETCH_ADDRESS), .out(multiplexer_5_out), .sel(nop));
  Multiplexer #(.width(5), .enable("false")) multiplexer_6 (
    .in0(multiplexer_4_out), .in1(jump_addr[27:23]), .out(multiplexer_6_out), .sel(Swinc));
  Multiplexer #(.width(32), .enable("false")) multiplexer_7 (
    .in0(data), .in1(multiplexer_2_out), .out(multiplexer_7_out), .sel(write_mf));
  // mem_main MEM: pin names not known; wires that end beside it: alu_out1, rt_data, MemWrite, CLOCK, OPUnit, mem_out
  assign bit_extender_1_out = {{16{1'b0}}, {jump_addr[17:8], func}};  // Bit_Extender bit_extender_1
  assign bit_extender_2_out = {{16{jump_addr[17]}}, {jump_addr[17:8], func}};  // Bit_Extender bit_extender_2
  Multiplexer #(.width(5)) multiplexer_8 (
    .in0(jump_addr[27:23]), .in1(jump_addr[22:18]), .out(multiplexer_8_out), .sel(shift_logic));  // open: en
  Multiplexer #(.width(32), .enable("false")) multiplexer_9 (
    .in0(multiplexer_7_out), .in1({jump_addr[31:28], PC_4}), .out(multiplexer_9_out), .sel(Link));
  Multiplexer #(.width(32), .enable("false")) multiplexer_10 (
    .in0(alu_out1), .in1(mem_out), .out(data), .sel(MemtoReg));
  Adder #(.width(32)) adder_1 (.a(FETCH_ADDRESS), .b(32'h4), .out({jump_addr[31:28], PC_4}));  // open: cin, cout
  Multiplexer #(.width(32), .enable("false")) multiplexer_11 (
    .in0(bit_extender_1_out), .in1(bit_extender_2_out), .out(imm), .sel(not_1_out));
  not not_1 (not_1_out, sign_logic);
  regfile_main main_1 (
    .Read_Register_1(multiplexer_8_out), .Read_Register_2(jump_addr[22:18]),
    .Write_Register(multiplexer_6_out), .Write_Data(multiplexer_9_out), .Write_Enable(RegWrite),
    .Clock(CLOCK), .Read_Data_1(rs_data), .Read_Data_2(rt_data), .s0_Value(s0_Value), .s1_Value(s1_Value),
    .s2_Value(s2_Value), .ra_Value(ra_Value));
  Shifter #(.width(32)) shifter_1 (.in(imm), .\dist (5'b00010), .out(shifter_1_out));
  Register #(.width(32)) HI (.D(alu_out2), .en(hi_logic), .Q(HI_Value), .clk(CLOCK));  // open: clr
  Adder #(.width(32)) adder_2 (.a({jump_addr[31:28], PC_4}), .b(shifter_1_out), .out(adder_2_out));  // open: cin, cout
  and and_1 (sign_logic, ~op_code[1], op_code[2], op_code[3], ~op_code[4], ~op_code[5]);  // AND_Gate
  and and_2 (and_2_out, ~func[2], ~func[3], ~func[4], ~func[5]);  // AND_Gate
  assign bit_extender_3_out = {{27{1'b0}}, jump_addr[12:8]};  // Bit_Extender bit_extender_3
  and and_3 (and_3_out, func[0], ~func[2], func[3], func[4], ~func[5]);  // AND_Gate
  Multiplexer #(.width(32), .enable("false")) multiplexer_12 (
    .in0({jump_addr[31:28], PC_4}), .in1(adder_2_out), .out(multiplexer_12_out), .sel(Branch));
  and and_4 (shift_logic, RType, and_2_out, nand_1_out);
  nand nand_1 (nand_1_out, func[0], ~func[1]);  // NAND_Gate
  Multiplexer #(.width(32), .enable("false")) multiplexer_13 (
    .in0(rt_data), .in1(bit_extender_3_out), .out(multiplexer_13_out), .sel(shift_logic));
  Shifter #(.width(32)) shifter_2 (.in(imm), .\dist (5'b10000), .out(shifter_2_out));
  Register #(.width(32)) LO (.D(alu_out1), .en(lo_logic), .Q(LO_Value), .clk(CLOCK));  // open: clr
  and and_5 (lo_logic, RType, and_3_out);
  control control_1 (
    .op_code(op_code), .func(func), .eq(eq), .RegDst(RegDst), .RType(RType), .Branch(Branch),
    .MemWrite(MemWrite), .MemRead(MemRead), .MemtoReg(MemtoReg), .OPUnit(OPUnit), .Lui(Lui), .ALUCtr(ALUCtr),
    .shifts(sh), .ALUSrc(ALUSrc), .RegWrite(RegWrite), .Jr(Jr), .Swinc(Swinc), .Link(Link), .Jump(Jump));
  Multiplexer #(.width(32), .enable("false")) multiplexer_14 (
    .in0(multiplexer_13_out), .in1(shifter_2_out), .out(multiplexer_14_out), .sel(Lui));
  and and_6 (hi_logic, lo_logic, func[1]);
  Multiplexer #(.width(32), .enable("false")) multiplexer_15 (
    .in0(multiplexer_12_out), .in1({jump_addr, func, 2'b00}), .out(multiplexer_15_out), .sel(Jump));
  Multiplexer #(.width(32), .enable("false")) multiplexer_16 (
    .in0(multiplexer_14_out), .in1(imm), .out(multiplexer_16_out), .sel(ALUSrc));
  // Probe on main_2_signed_overflow
  alu_main main_2 (
    .Switch(ALUCtr), .X(rs_data), .Equal(eq), .Result(alu_out1), .Signed_Overflow(main_2_signed_overflow),
    .Y(multiplexer_16_out), .Result_2(alu_out2));
  and and_7 (and_7_out, ~func[0], ~func[2], ~func[3], func[4], ~func[5]);  // AND_Gate
  and and_8 (mf_logic, func[1], write_mf);
  Multiplexer #(.width(32), .enable("false")) multiplexer_17 (
    .in0(multiplexer_15_out), .in1(rs_data), .out(next_pc), .sel(Jr));
  and and_9 (write_mf, RType, and_7_out);

  // Other names for the same wires on the sheet: clk = CLOCK; fetch_addr[31:0] = FETCH_ADDRESS; hi[31:0] = HI_Value;
  //   jump_addr[7:2] = func; shamt[4:0] = jump_addr[12:8]; rd[4:0] = jump_addr[17:13]; rt[4:0] = jump_addr[22:18];
  //   rs[4:0] = jump_addr[27:23]; lo[31:0] = LO_Value; PC_4[31:28] = jump_addr[31:28]; ra[31:0] = ra_Value;
  //   s0[31:0] = s0_Value; s1[31:0] = s1_Value; s2[31:0] = s2_Value; wd[31:0] = rt_data

  // Notes on the sheet:
  //   Output
  //   Decode / Register Read
  //   These are outputs/inputs from run.circ
  //   Inputs
  //   Memory & Register Write
  //   Instruction Fetch
  //   Next PC Logic
  //   These are DEBUG/TEST outputs from your circuit.
  //   Execute
  //   Hi/Lo Logic
  //   Control Unit
endmodule

module control (
  input  [5:0] op_code,
  input  [5:0] func,
  input  eq,
  output RegDst,
  output RType,
  output Branch,
  output MemWrite,
  output MemRead,
  output MemtoReg,
  output [2:0] OPUnit,
  output Lui,
  output [3:0] ALUCtr,
  output shifts,
  output ALUSrc,
  output RegWrite,
  output Jr,
  output Swinc,
  output Link,
  output Jump
);

  wire and_1_out, and_2_out, and_3_out, and_4_out, and_5_out, and_6_out, and_16_out, and_17_out, and_20_out,
       and_21_out, and_22_out, and_23_out, and_33_out, and_34_out, and_35_out, and_36_out, and_37_out,
       and_38_out, and_39_out, and_40_out, and_47_out, and_51_out, and_52_out, and_53_out, and_62_out,
       and_63_out, and_64_out, comparator_1_eq, comparator_2_eq, comparator_3_eq, comparator_4_eq,
       comparator_5_eq, comparator_6_eq, comparator_7_eq, comparator_8_eq, comparator_9_eq, comparator_10_eq,
       comparator_11_eq, comparator_12_eq, comparator_13_eq, comparator_14_eq, comparator_15_eq,
       comparator_16_eq, comparator_17_eq, comparator_18_eq, comparator_19_eq, comparator_20_eq,
       comparator_21_eq, comparator_22_eq, comparator_23_eq, comparator_24_eq, comparator_26_eq,
       comparator_27_eq, comparator_28_eq, comparator_29_eq, comparator_30_eq, comparator_31_eq,
       comparator_32_eq, comparator_33_eq, comparator_34_eq, comparator_35_eq, comparator_37_eq,
       comparator_38_eq, comparator_39_eq, nand_1_out, nand_2_out, nand_4_out, nand_5_out, or_1_out,
       or_8_out, s, xnor_1_out;
  wire [2:0] multiplexer_1_out;
  wire [3:0] add, addi, addiu, addu, \and , andi, beq, beqal, bit_extender_1_out, bit_extender_2_out,
       bit_extender_3_out, bit_extender_4_out, bit_extender_5_out, bit_extender_6_out, bit_extender_7_out,
       bit_extender_8_out, bit_extender_9_out, bit_extender_10_out, bit_extender_11_out, bit_extender_12_out,
       bit_extender_13_out, bit_extender_14_out, bit_extender_15_out, bit_extender_16_out,
       bit_extender_17_out, bit_extender_18_out, bit_extender_19_out, bit_extender_20_out,
       bit_extender_21_out, bit_extender_22_out, bit_extender_23_out, bit_extender_24_out,
       bit_extender_25_out, bit_extender_26_out, bit_extender_27_out, bit_extender_28_out,
       bit_extender_29_out, bit_extender_30_out, bit_extender_31_out, bit_extender_32_out,
       bit_extender_33_out, bit_extender_34_out, bit_extender_35_out, bne, divu, j, jal, jr_t, lb, lbu, lhu,
       lui_t, lw, mfhi, mflo, multu, \or , or_5_out, or_7_out, ori, sb, sh, sll, slt, slti, sltu, sra, srl,
       sub, subu, sw, swinc_t;

  Comparator #(.width(6)) comparator_1 (.a(func), .b(6'b100000), .eq(comparator_1_eq));  // open: gt, lt
  Comparator #(.width(6)) comparator_2 (.a(func), .b(6'b100001), .eq(comparator_2_eq));  // open: gt, lt
  Comparator #(.width(6)) comparator_3 (.a(func), .b(6'b100100), .eq(comparator_3_eq));  // open: gt, lt
  Comparator #(.width(6)) comparator_4 (.a(func), .b(6'b011011), .eq(comparator_4_eq));  // open: gt, lt
  assign bit_extender_1_out = {{3{and_1_out}}, and_1_out};  // Bit_Extender bit_extender_1
  and and_1 (and_1_out, RType, comparator_1_eq);
  assign bit_extender_2_out = {{3{and_2_out}}, and_2_out};  // Bit_Extender bit_extender_2
  and and_2 (and_2_out, RType, comparator_2_eq);
  and and_3 (and_3_out, RType, comparator_3_eq);
  assign bit_extender_3_out = {{3{and_3_out}}, and_3_out};  // Bit_Extender bit_extender_3
  and and_4 (and_4_out, RType, comparator_4_eq);
  assign bit_extender_4_out = {{3{and_4_out}}, and_4_out};  // Bit_Extender bit_extender_4
  assign bit_extender_5_out = {{3{comparator_5_eq}}, comparator_5_eq};  // Bit_Extender bit_extender_5
  Comparator #(.width(6)) comparator_5 (.a(op_code), .b(6'b000010), .eq(comparator_5_eq));  // open: gt, lt
  assign bit_extender_6_out = {{3{comparator_6_eq}}, comparator_6_eq};  // Bit_Extender bit_extender_6
  Comparator #(.width(6)) comparator_6 (.a(op_code), .b(6'b001000), .eq(comparator_6_eq));  // open: gt, lt
  Comparator #(.width(6)) comparator_7 (.a(op_code), .b(6'b001001), .eq(comparator_7_eq));  // open: gt, lt
  assign bit_extender_7_out = {{3{comparator_7_eq}}, comparator_7_eq};  // Bit_Extender bit_extender_7
  Comparator #(.width(6)) comparator_8 (.a(op_code), .b(6'b100100), .eq(comparator_8_eq));  // open: gt, lt
  assign bit_extender_8_out = {{3{comparator_8_eq}}, comparator_8_eq};  // Bit_Extender bit_extender_8
  assign bit_extender_9_out = {{3{comparator_9_eq}}, comparator_9_eq};  // Bit_Extender bit_extender_9
  Comparator #(.width(6)) comparator_9 (.a(op_code), .b(6'b000100), .eq(comparator_9_eq));  // open: gt, lt
  Comparator #(.width(6)) comparator_10 (.a(func), .b(6'b001000), .eq(comparator_10_eq));  // open: gt, lt
  Comparator #(.width(6)) comparator_11 (.a(op_code), .b(6'b000010), .eq(comparator_11_eq));  // open: gt, lt
  Comparator #(.width(6)) comparator_12 (.a(op_code), .b(6'b000011), .eq(comparator_12_eq));  // open: gt, lt
  and and_5 (and_5_out, ~op_code[2], xnor_1_out);  // AND_Gate
  xnor xnor_1 (xnor_1_out, op_code[0], op_code[1]);
  nand nand_1 (nand_1_out, op_code[1], ~op_code[0]);  // NAND_Gate
  and and_6 (and_6_out, nand_1_out, op_code[2]);
  assign add = bit_extender_1_out & 4'b0101;  // AND_Gate and_7, 4 bits wide
  assign addu = bit_extender_2_out & 4'b0110;  // AND_Gate and_8, 4 bits wide
  assign \and  = bit_extender_3_out & 4'b1001;  // AND_Gate and_9, 4 bits wide
  assign divu = bit_extender_4_out & 4'b0100;  // AND_Gate and_10, 4 bits wide
  assign j = bit_extender_5_out & 4'b0000;  // AND_Gate and_11, 4 bits wide
  assign addi = bit_extender_6_out & 4'b0101;  // AND_Gate and_12, 4 bits wide
  assign addiu = bit_extender_7_out & 4'b0110;  // AND_Gate and_13, 4 bits wide
  assign andi = bit_extender_8_out & 4'b1001;  // AND_Gate and_14, 4 bits wide
  assign beq = bit_extender_9_out & 4'b0000;  // AND_Gate and_15, 4 bits wide
  and and_16 (and_16_out, ~op_code[3], op_code[4], op_code[5]);  // AND_Gate
  and and_17 (and_17_out, ~op_code[4], op_code[5]);  // AND_Gate
  and and_18 (Jr, RType, comparator_10_eq);
  or or_1 (or_1_out, and_5_out, and_6_out);
  or or_2 (ALUSrc, and_16_out, and_17_out);
  or or_3 (Jump, comparator_11_eq, comparator_12_eq);
  Comparator #(.width(6)) comparator_13 (.a(func), .b(6'b011001), .eq(comparator_13_eq));  // open: gt, lt
  Comparator #(.width(6)) comparator_14 (.a(func), .b(6'b010000), .eq(comparator_14_eq));  // open: gt, lt
  Comparator #(.width(6)) comparator_15 (.a(func), .b(6'b010010), .eq(comparator_15_eq));  // open: gt, lt
  Comparator #(.width(6)) comparator_16 (.a(func), .b(6'b100101), .eq(comparator_16_eq));  // open: gt, lt
  Comparator #(.width(6)) comparator_17 (.a(op_code), .b(6'b000011), .eq(comparator_17_eq));  // open: gt, lt
  Comparator #(.width(6)) comparator_18 (.a(op_code), .b(6'b010100), .eq(comparator_18_eq));  // open: gt, lt
  Comparator #(.width(6)) comparator_19 (.a(op_code), .b(6'b000101), .eq(comparator_19_eq));  // open: gt, lt
  Comparator #(.width(6)) comparator_20 (.a(op_code), .b(6'b100000), .eq(comparator_20_eq));  // open: gt, lt
  Comparator #(.width(6)) comparator_21 (.a(op_code), .b(6'b100100), .eq(comparator_21_eq));  // open: gt, lt
  and and_19 (MemtoReg, ~op_code[3], ~op_code[4], op_code[5], or_1_out);  // AND_Gate
  assign bit_extender_10_out = {{3{and_20_out}}, and_20_out};  // Bit_Extender bit_extender_10
  and and_20 (and_20_out, RType, comparator_13_eq);
  assign bit_extender_11_out = {{3{and_21_out}}, and_21_out};  // Bit_Extender bit_extender_11
  and and_21 (and_21_out, RType, comparator_14_eq);
  assign bit_extender_12_out = {{3{and_22_out}}, and_22_out};  // Bit_Extender bit_extender_12
  and and_22 (and_22_out, RType, comparator_15_eq);
  assign bit_extender_13_out = {{3{and_23_out}}, and_23_out};  // Bit_Extender bit_extender_13
  and and_23 (and_23_out, RType, comparator_16_eq);
  assign bit_extender_14_out = {{3{comparator_17_eq}}, comparator_17_eq};  // Bit_Extender bit_extender_14
  assign bit_extender_15_out = {{3{comparator_18_eq}}, comparator_18_eq};  // Bit_Extender bit_extender_15
  assign bit_extender_16_out = {{3{comparator_19_eq}}, comparator_19_eq};  // Bit_Extender bit_extender_16
  assign bit_extender_17_out = {{3{comparator_20_eq}}, comparator_20_eq};  // Bit_Extender bit_extender_17
  assign bit_extender_18_out = {{3{comparator_21_eq}}, comparator_21_eq};  // Bit_Extender bit_extender_18
  nand nand_2 (nand_2_out, op_code[0], op_code[4]);
  or or_4 (MemRead, MemtoReg, Lui);
  assign multu = bit_extender_10_out & 4'b0011;  // AND_Gate and_24, 4 bits wide
  assign mfhi = bit_extender_11_out & 4'b0000;  // AND_Gate and_25, 4 bits wide
  assign mflo = bit_extender_12_out & 4'b0000;  // AND_Gate and_26, 4 bits wide
  assign \or  = bit_extender_13_out & 4'b1010;  // AND_Gate and_27, 4 bits wide
  assign jal = bit_extender_14_out & 4'b0000;  // AND_Gate and_28, 4 bits wide
  assign beqal = bit_extender_15_out & 4'b0000;  // AND_Gate and_29, 4 bits wide
  assign bne = bit_extender_16_out & 4'b0000;  // AND_Gate and_30, 4 bits wide
  assign lb = bit_extender_17_out & 4'b0101;  // AND_Gate and_31, 4 bits wide
  assign lbu = bit_extender_18_out & 4'b0110;  // AND_Gate and_32, 4 bits wide
  assign or_5_out = add | addu | \and  | divu | multu | \or  | slt | sltu | sll | sra | srl | sub | subu | addi;  // OR_Gate or_5, 4 bits wide
  and and_33 (and_33_out, ~op_code[0], ~op_code[1], op_code[2], op_code[3], op_code[4], op_code[5]);  // AND_Gate
  and and_34 (and_34_out, ~op_code[0], ~op_code[1], op_code[2], ~op_code[3], op_code[4], ~op_code[5]);  // AND_Gate
  nand nand_3 (RType, op_code[0], op_code[1], op_code[2], op_code[3], op_code[4], op_code[5]);
  and and_35 (and_35_out, ~op_code[1], op_code[2], ~op_code[3], ~op_code[5], nand_2_out);  // AND_Gate
  Comparator #(.width(6)) comparator_22 (.a(func), .b(6'b101010), .eq(comparator_22_eq));  // open: gt, lt
  Comparator #(.width(6)) comparator_23 (.a(func), .b(6'b101011), .eq(comparator_23_eq));  // open: gt, lt
  Comparator #(.width(6)) comparator_24 (.a(op_code), .b(6'b100101), .eq(comparator_24_eq));  // open: gt, lt
  Comparator #(.width(6)) comparator_25 (.a(op_code), .b(6'b001111), .eq(Lui));  // open: gt, lt
  Comparator #(.width(6)) comparator_26 (.a(op_code), .b(6'b100011), .eq(comparator_26_eq));  // open: gt, lt
  Comparator #(.width(6)) comparator_27 (.a(op_code), .b(6'b001101), .eq(comparator_27_eq));  // open: gt, lt
  or or_6 (Link, and_33_out, and_34_out);
  and and_36 (and_36_out, ~op_code[0], eq);  // AND_Gate
  nand nand_4 (nand_4_out, ~op_code[0], op_code[1]);  // NAND_Gate
  and and_37 (and_37_out, RType, comparator_22_eq);
  assign bit_extender_19_out = {{3{and_37_out}}, and_37_out};  // Bit_Extender bit_extender_19
  and and_38 (and_38_out, RType, comparator_23_eq);
  assign bit_extender_20_out = {{3{and_38_out}}, and_38_out};  // Bit_Extender bit_extender_20
  assign bit_extender_21_out = {{3{comparator_24_eq}}, comparator_24_eq};  // Bit_Extender bit_extender_21
  assign bit_extender_22_out = {{3{Lui}}, Lui};  // Bit_Extender bit_extender_22
  assign bit_extender_23_out = {{3{comparator_26_eq}}, comparator_26_eq};  // Bit_Extender bit_extender_23
  assign bit_extender_24_out = {{3{comparator_27_eq}}, comparator_27_eq};  // Bit_Extender bit_extender_24
  and and_39 (and_39_out, op_code[0], ~eq);  // AND_Gate
  and and_40 (and_40_out, ~op_code[2], op_code[3], ~op_code[4], op_code[5], nand_4_out);  // AND_Gate
  assign slt = bit_extender_19_out & 4'b1011;  // AND_Gate and_41, 4 bits wide
  assign sltu = bit_extender_20_out & 4'b1100;  // AND_Gate and_42, 4 bits wide
  assign lhu = bit_extender_21_out & 4'b0110;  // AND_Gate and_43, 4 bits wide
  assign lui_t = bit_extender_22_out & 4'b0101;  // AND_Gate and_44, 4 bits wide
  assign lw = bit_extender_23_out & 4'b0101;  // AND_Gate and_45, 4 bits wide
  assign ori = bit_extender_24_out & 4'b1010;  // AND_Gate and_46, 4 bits wide
  nand nand_5 (nand_5_out, ~op_code[4], op_code[5]);  // NAND_Gate
  Comparator #(.width(6)) comparator_28 (.a(op_code), .b(6'b101100), .eq(comparator_28_eq));  // open: gt, lt
  assign or_7_out = addiu | andi | lb | lbu | lhu | lui_t | lw | ori | slti | sb | sh | sw | swinc_t;  // OR_Gate or_7, 4 bits wide
  and and_47 (and_47_out, ALUSrc, ~MemWrite);  // AND_Gate
  and and_48 (RegDst, RType, nand_5_out);
  or or_8 (or_8_out, and_36_out, and_39_out);
  or or_9 (MemWrite, and_40_out, comparator_28_eq);
  Comparator #(.width(6)) comparator_29 (.a(func), .b(6'b100010), .eq(comparator_29_eq));  // open: gt, lt
  Comparator #(.width(6)) comparator_30 (.a(func), .b(6'b100011), .eq(comparator_30_eq));  // open: gt, lt
  Comparator #(.width(6)) comparator_31 (.a(func), .b(6'b001000), .eq(comparator_31_eq));  // open: gt, lt
  Comparator #(.width(6)) comparator_32 (.a(op_code), .b(6'b001010), .eq(comparator_32_eq));  // open: gt, lt
  Comparator #(.width(6)) comparator_33 (.a(op_code), .b(6'b101000), .eq(comparator_33_eq));  // open: gt, lt
  Comparator #(.width(6)) comparator_34 (.a(op_code), .b(6'b101001), .eq(comparator_34_eq));  // open: gt, lt
  Comparator #(.width(6)) comparator_35 (.a(op_code), .b(6'b101011), .eq(comparator_35_eq));  // open: gt, lt
  Comparator #(.width(6)) comparator_36 (.a(op_code), .b(6'b101100), .eq(s));  // open: gt, lt
  or or_10 (RegWrite, RegDst, Link, Swinc, and_47_out);
  and and_49 (Swinc, ~op_code[0], ~op_code[1], op_code[2], op_code[3], ~op_code[4], op_code[5]);  // AND_Gate
  and and_50 (Branch, and_35_out, or_8_out);
  assign bit_extender_25_out = {{3{and_51_out}}, and_51_out};  // Bit_Extender bit_extender_25
  and and_51 (and_51_out, RType, comparator_29_eq);
  assign bit_extender_26_out = {{3{and_52_out}}, and_52_out};  // Bit_Extender bit_extender_26
  and and_52 (and_52_out, RType, comparator_30_eq);
  and and_53 (and_53_out, RType, comparator_31_eq);
  assign bit_extender_27_out = {{3{and_53_out}}, and_53_out};  // Bit_Extender bit_extender_27
  assign bit_extender_28_out = {{3{comparator_32_eq}}, comparator_32_eq};  // Bit_Extender bit_extender_28
  assign bit_extender_29_out = {{3{comparator_33_eq}}, comparator_33_eq};  // Bit_Extender bit_extender_29
  assign bit_extender_30_out = {{3{comparator_34_eq}}, comparator_34_eq};  // Bit_Extender bit_extender_30
  assign bit_extender_31_out = {{3{comparator_35_eq}}, comparator_35_eq};  // Bit_Extender bit_extender_31
  assign bit_extender_32_out = {{3{s}}, s};  // Bit_Extender bit_extender_32
  assign ALUCtr = or_5_out | or_7_out;  // OR_Gate or_11, 4 bits wide
  assign sub = bit_extender_25_out & 4'b0111;  // AND_Gate and_54, 4 bits wide
  assign subu = bit_extender_26_out & 4'b1000;  // AND_Gate and_55, 4 bits wide
  assign jr_t = bit_extender_27_out & 4'b0000;  // AND_Gate and_56, 4 bits wide
  assign slti = bit_extender_28_out & 4'b1011;  // AND_Gate and_57, 4 bits wide
  assign sb = bit_extender_29_out & 4'b0101;  // AND_Gate and_58, 4 bits wide
  assign sh = bit_extender_30_out & 4'b0101;  // AND_Gate and_59, 4 bits wide
  assign sw = bit_extender_31_out & 4'b0101;  // AND_Gate and_60, 4 bits wide
  assign swinc_t = bit_extender_32_out & 4'b0101;  // AND_Gate and_61, 4 bits wide
  Multiplexer #(.width(3)) multiplexer_1 (.in0(3'b000), .in1(3'b100), .out(multiplexer_1_out), .sel(s));  // open: en
  and and_62 (and_62_out, RType, comparator_37_eq);
  Comparator #(.width(6)) comparator_37 (.a(func), .b(6'b000010), .eq(comparator_37_eq));  // open: gt, lt
  and and_63 (and_63_out, RType, comparator_38_eq);
  Comparator #(.width(6)) comparator_38 (.a(func), .b({6{1'b0}}), .eq(comparator_38_eq));  // open: gt, lt
  and and_64 (and_64_out, RType, comparator_39_eq);
  Comparator #(.width(6)) comparator_39 (.a(func), .b(6'b000011), .eq(comparator_39_eq));  // open: gt, lt
  or or_12 (shifts, and_63_out, and_64_out, and_62_out);
  assign bit_extender_33_out = {{3{and_62_out}}, and_62_out};  // Bit_Extender bit_extender_33
  assign bit_extender_34_out = {{3{and_63_out}}, and_63_out};  // Bit_Extender bit_extender_34
  assign bit_extender_35_out = {{3{and_64_out}}, and_64_out};  // Bit_Extender bit_extender_35
  Multiplexer #(.select(3), .width(3)) multiplexer_2 (
    .in0(3'b001), .in1(3'b011), .in3(3'b100), .in4(multiplexer_1_out), .in5(3'b010), .out(OPUnit),
    .sel(op_code[2:0]));  // open: in2, in6, in7, en
  assign srl = bit_extender_33_out & 4'b0001;  // AND_Gate and_65, 4 bits wide
  assign sll = bit_extender_34_out & 4'b0000;  // AND_Gate and_66, 4 bits wide
  assign sra = bit_extender_35_out & 4'b0010;  // AND_Gate and_67, 4 bits wide
  Multiplexer #(.select(2), .width(32)) multiplexer_3 ();  // open: in0, in1, in2, in3, out, sel, en

  // Other names for the same wires on the sheet: lui_mem = Lui; op0 = op_code[0]; op1 = op_code[1]; op2 = op_code[2];
  //   op3 = op_code[3]; op4 = op_code[4]; op5 = op_code[5]; swinc_write = Swinc

  // Notes on the sheet:
  //   Inputs
  //   Memory
  //   ALUCtr
  //   ALUSrc
  //   RegWrite
  //   RegDst
  //   Branch
endmodule
