// Logisim project regfile.circ as structural Verilog: 1 circuit, main circuit main
module main (
  input  [4:0] Read_Register_1,
  input  [4:0] Read_Register_2,
  input  [4:0] Write_Register,
  input  [31:0] Write_Data,
  input  Write_Enable,
  input  Clock,
  output [31:0] s0_Value,
  output [31:0] s1_Value,
  output [31:0] s2_Value,
  output [31:0] ra_Value,
  output [31:0] Read_Data_1,
  output [31:0] Read_Data_2
);

  wire w_a0, w_a1, w_a2, w_a3, w_at, w_fp, w_gp, w_k0, w_k1, w_ra, w_s0, w_s1, w_s2, w_s3, w_s4, w_s5, w_s6,
       w_s7, w_sp, w_t0, w_t1, w_t2, w_t3, w_t4, w_t5, w_t6, w_t7, w_t8, w_t9, w_v0, w_v1;
  wire [31:0] a0, a0_t, a1, a1_t, a2, a2_t, a3, a3_t, at, at_t, fp, fp_t, gp, gp_t, k0, k0_t, k1, k1_t, ra,
       s0, s1, s2, s3, s3_t, s4, s4_t, s5, s5_t, s6, s6_t, s7, s7_t, sp, sp_t, t0, t0_t, t1, t1_t, t2, t2_t,
       t3, t3_t, t4, t4_t, t5, t5_t, t6, t6_t, t7, t7_t, t8, t8_t, t9, t9_t, v0, v0_t, v1, v1_t;

  Register #(.width(32)) register_1 (.D(t5), .en(w_t5), .Q(t5_t), .clk(Clock));  // open: clr
  Register #(.width(32)) register_2 (.D(t6), .en(w_t6), .Q(t6_t), .clk(Clock));  // open: clr
  Register #(.width(32)) register_3 (.D(t7), .en(w_t7), .Q(t7_t), .clk(Clock));  // open: clr
  Register #(.width(32)) register_4 (.D(at), .en(w_at), .Q(at_t), .clk(Clock));  // open: clr
  Register #(.width(32)) register_5 (.D(v0), .en(w_v0), .Q(v0_t), .clk(Clock));  // open: clr
  Register #(.width(32)) register_6 (.D(v1), .en(w_v1), .Q(v1_t), .clk(Clock));  // open: clr
  Register #(.width(32)) register_7 (.D(a0), .en(w_a0), .Q(a0_t), .clk(Clock));  // open: clr
  Register #(.width(32)) register_8 (.D(a1), .en(w_a1), .Q(a1_t), .clk(Clock));  // open: clr
  Register #(.width(32)) register_9 (.D(a2), .en(w_a2), .Q(a2_t), .clk(Clock));  // open: clr
  Register #(.width(32)) register_10 (.D(a3), .en(w_a3), .Q(a3_t), .clk(Clock));  // open: clr
  Register #(.width(32)) register_11 (.D(t0), .en(w_t0), .Q(t0_t), .clk(Clock));  // open: clr
  Register #(.width(32)) register_12 (.D(t1), .en(w_t1), .Q(t1_t), .clk(Clock));  // open: clr
  Register #(.width(32)) register_13 (.D(t2), .en(w_t2), .Q(t2_t), .clk(Clock));  // open: clr
  Register #(.width(32)) register_14 (.D(t3), .en(w_t3), .Q(t3_t), .clk(Clock));  // open: clr
  Register #(.width(32)) register_15 (.D(t4), .en(w_t4), .Q(t4_t), .clk(Clock));  // open: clr
  Register #(.width(32)) register_16 (.D(s0), .en(w_s0), .Q(s0_Value), .clk(Clock));  // open: clr
  Register #(.width(32)) register_17 (.D(s1), .en(w_s1), .Q(s1_Value), .clk(Clock));  // open: clr
  Register #(.width(32)) register_18 (.D(s2), .en(w_s2), .Q(s2_Value), .clk(Clock));  // open: clr
  Register #(.width(32)) register_19 (.D(s3), .en(w_s3), .Q(s3_t), .clk(Clock));  // open: clr
  Register #(.width(32)) register_20 (.D(s4), .en(w_s4), .Q(s4_t), .clk(Clock));  // open: clr
  Register #(.width(32)) register_21 (.D(s5), .en(w_s5), .Q(s5_t), .clk(Clock));  // open: clr
  Register #(.width(32)) register_22 (.D(s6), .en(w_s6), .Q(s6_t), .clk(Clock));  // open: clr
  Register #(.width(32)) register_23 (.D(s7), .en(w_s7), .Q(s7_t), .clk(Clock));  // open: clr
  Register #(.width(32)) register_24 (.D(t8), .en(w_t8), .Q(t8_t), .clk(Clock));  // open: clr
  Register #(.width(32)) register_25 (.D(t9), .en(w_t9), .Q(t9_t), .clk(Clock));  // open: clr
  Register #(.width(32)) register_26 (.D(k0), .en(w_k0), .Q(k0_t), .clk(Clock));  // open: clr
  Register #(.width(32)) register_27 (.D(k1), .en(w_k1), .Q(k1_t), .clk(Clock));  // open: clr
  Register #(.width(32)) register_28 (.D(gp), .en(w_gp), .Q(gp_t), .clk(Clock));  // open: clr
  Register #(.width(32)) register_29 (.D(sp), .en(w_sp), .Q(sp_t), .clk(Clock));  // open: clr
  Register #(.width(32)) register_30 (.D(fp), .en(w_fp), .Q(fp_t), .clk(Clock));  // open: clr
  Register #(.width(32)) register_31 (.D(ra), .en(w_ra), .Q(ra_Value), .clk(Clock));  // open: clr
  Multiplexer #(.select(5), .width(32)) multiplexer_1 (
    .in0({32{1'b0}}), .in1(at_t), .in2(v0_t), .in3(v1_t), .in4(a0_t), .in5(a1_t), .in6(a2_t), .in7(a3_t),
    .in8(t0_t), .in9(t1_t), .in10(t2_t), .in11(t3_t), .in12(t4_t), .in13(t5_t), .in14(t6_t), .in15(t7_t),
    .in16(s0_Value), .in17(s1_Value), .in18(s2_Value), .in19(s3_t), .in20(s4_t), .in21(s5_t), .in22(s6_t),
    .in23(s7_t), .in24(t8_t), .in25(t9_t), .in26(k0_t), .in27(k1_t), .in28(gp_t), .in29(sp_t), .in30(fp_t),
    .in31(ra_Value), .out(Read_Data_1), .sel(Read_Register_1));  // open: en
  Multiplexer #(.select(5), .width(32)) multiplexer_2 (
    .in0({32{1'b0}}), .in1(at_t), .in2(v0_t), .in3(v1_t), .in4(a0_t), .in5(a1_t), .in6(a2_t), .in7(a3_t),
    .in8(t0_t), .in9(t1_t), .in10(t2_t), .in11(t3_t), .in12(t4_t), .in13(t5_t), .in14(t6_t), .in15(t7_t),
    .in16(s0_Value), .in17(s1_Value), .in18(s2_Value), .in19(s3_t), .in20(s4_t), .in21(s5_t), .in22(s6_t),
    .in23(s7_t), .in24(t8_t), .in25(t9_t), .in26(k0_t), .in27(k1_t), .in28(gp_t), .in29(sp_t), .in30(fp_t),
    .in31(ra_Value), .out(Read_Data_2), .sel(Read_Register_2));  // open: en
  Demultiplexer #(.select(5), .width(32)) demultiplexer_1 (
    .out1(at), .out2(v0), .out3(v1), .out4(a0), .out5(a1), .out6(a2), .out7(a3), .out8(t0), .out9(t1),
    .out10(t2), .out11(t3), .out12(t4), .out13(t5), .out14(t6), .out15(t7), .out16(s0), .out17(s1),
    .out18(s2), .out19(s3), .out20(s4), .out21(s5), .out22(s6), .out23(s7), .out24(t8), .out25(t9),
    .out26(k0), .out27(k1), .out28(gp), .out29(sp), .out30(fp), .out31(ra), .in(Write_Data),
    .sel(Write_Register), .en(Write_Enable));  // open: out0
  Demultiplexer #(.select(5)) demultiplexer_2 (
    .out1(w_at), .out2(w_v0), .out3(w_v1), .out4(w_a0), .out5(w_a1), .out6(w_a2), .out7(w_a3), .out8(w_t0),
    .out9(w_t1), .out10(w_t2), .out11(w_t3), .out12(w_t4), .out13(w_t5), .out14(w_t6), .out15(w_t7),
    .out16(w_s0), .out17(w_s1), .out18(w_s2), .out19(w_s3), .out20(w_s4), .out21(w_s5), .out22(w_s6),
    .out23(w_s7), .out24(w_t8), .out25(w_t9), .out26(w_k0), .out27(w_k1), .out28(w_gp), .out29(w_sp),
    .out30(w_fp), .out31(w_ra), .in(1'b1), .sel(Write_Register), .en(Write_Enable));  // open: out0

  // Other names for the same wires on the sheet: clk = Clock; ra_t[31:0] = ra_Value; read_data1[31:0] = Read_Data_1;
  //   read_data2[31:0] = Read_Data_2; read_reg1[4:0] = Read_Register_1; read_reg2[4:0] = Read_Register_2;
  //   s0_t[31:0] = s0_Value; s1_t[31:0] = s1_Value; s2_t[31:0] = s2_Value; write_en = Write_Enable;
  //   write_reg[4:0] = Write_Register

  // Notes on the sheet:
  //   INPUTS to your circuit
  //   DON'T CHANGE THE LOCATIONS OF THE INPUTS AND OUTPUTS!
  //   These are DEBUG/TEST outputs from your circuit.
  //   OUTPUTS from your circuit
endmodule
